// Logisim project GTI.circ as structural Verilog: 10 circuits, main circuit main
module main (
  input  x1,
  input  x0,
  input  y1,
  input  y0,
  input  z1,
  input  z0,
  output out_7,
  output out_8,
  output out_9,
  output out_10
);

  wire fa_1_c_out, fa_1_s, fa_2_s, ha_2_s;

  FA fa_1 (.C_in(z1), .B(y1), .A(x1), .C_out(fa_1_c_out), .S(fa_1_s));
  HA ha_1 (.B(ha_2_s), .A(fa_1_s), .C(out_8), .S(out_7));
  FA fa_2 (.C_in(z0), .B(y0), .A(x0), .C_out(out_10), .S(fa_2_s));
  HA ha_2 (.B(fa_2_s), .A(fa_1_c_out), .C(out_9), .S(ha_2_s));
endmodule

module HA (
  input  B,
  input  A,
  output C,
  output S
);

  and and_1 (C, B, A);
  xor xor_1 (S, B, A);
endmodule

module FA (
  input  C_in,
  input  B,
  input  A,
  output C_out,
  output S
);

  wire and_1_out, and_2_out, xor_1_out;

  and and_1 (and_1_out, A, B);
  and and_2 (and_2_out, C_in, xor_1_out);
  or or_1 (C_out, and_1_out, and_2_out);
  xor xor_1 (xor_1_out, B, A);
  xor xor_2 (S, C_in, xor_1_out);
endmodule

module SR_flipflop (
  input  S,
  input  R,
  output Q,
  output NOT_Q
);

  nor nor_1 (NOT_Q, S, Q);
  nor nor_2 (Q, NOT_Q, R);
endmodule

module SR_clk (
  input  S,
  input  R,
  output NOT_Q,
  output Q
);

  wire and_1_out, and_2_out, clock_1_out;

  Clock clock_1 (.out(clock_1_out));
  and and_1 (and_1_out, S, clock_1_out);
  and and_2 (and_2_out, clock_1_out, R);
  nor nor_1 (NOT_Q, and_1_out, Q);
  nor nor_2 (Q, NOT_Q, and_2_out);
endmodule

module Addierwerk (
  input  S,
  input  Y2,
  input  X2,
  input  Y1,
  input  X1,
  input  Y0,
  input  X0,
  output out_8,
  output out_9,
  output out_10
);

  wire fa_2_c_out, fa_3_c_out, xor_1_out, xor_2_out, xor_3_out;

  xor xor_1 (xor_1_out, S, Y2);
  FA fa_1 (.C_in(fa_2_c_out), .B(X2), .A(xor_1_out), .S(out_8));  // open: C_out
  xor xor_2 (xor_2_out, S, Y1);
  FA fa_2 (.C_in(fa_3_c_out), .B(X1), .A(xor_2_out), .C_out(fa_2_c_out), .S(out_9));
  xor xor_3 (xor_3_out, S, Y0);
  FA fa_3 (.C_in(S), .B(X0), .A(xor_3_out), .C_out(fa_3_c_out), .S(out_10));
endmodule

module Addierwerkalternative (
  input  S,
  input  Y0,
  input  X0,
  input  Y1,
  input  X1,
  input  Y2,
  input  X2,
  output R0,
  output R1,
  output R2
);

  wire adder_1_cout, adder_2_cout, xor_1_out, xor_2_out, xor_3_out;

  xor xor_1 (xor_1_out, S, Y0);
  xor xor_2 (xor_2_out, S, Y1);
  xor xor_3 (xor_3_out, S, Y2);
  Adder #(.width(1)) adder_1 (.a(xor_1_out), .b(X0), .out(R0), .cin(S), .cout(adder_1_cout));
  Adder #(.width(1)) adder_2 (.a(xor_2_out), .b(X1), .out(R1), .cin(adder_1_cout), .cout(adder_2_cout));
  Adder #(.width(1)) adder_3 (.a(xor_3_out), .b(X2), .out(R2), .cin(adder_2_cout));  // open: cout
endmodule

module D_FlipFlop (
  input  Gate_G,
  input  Data_D,
  output Q
);

  wire and_1_out, and_2_out, not_1_out, or_1_out, or_2_out;

  and and_1 (and_1_out, Gate_G, Data_D);
  and and_2 (and_2_out, ~Data_D, Gate_G);  // AND_Gate
  or or_1 (or_1_out, and_1_out, Q);
  not not_1 (not_1_out, or_1_out);
  or or_2 (or_2_out, not_1_out, and_2_out);
  not not_2 (Q, or_2_out);
endmodule

module JK_FlipFlop (
  input  J,
  input  K,
  output Q
);

  wire and_1_out, and_2_out, sr_flipflop_1_not_q;

  and and_1 (and_1_out, sr_flipflop_1_not_q, J);
  and and_2 (and_2_out, K, Q);
  SR_flipflop sr_flipflop_1 (.S(and_1_out), .R(and_2_out), .Q(Q), .NOT_Q(sr_flipflop_1_not_q));
endmodule

module A4 (
);

  wire and_1_out, and_2_out, and_3_out, and_4_out, clock_1_out, j_k_ff_1_q, j_k_ff_2_q, j_k_ff_3_q,
       not_1_out, or_1_out, or_2_out;

  Clock clock_1 (.out(clock_1_out));
  J_K_Flip_Flop j_k_ff_1 (.J(or_1_out), .clk(clock_1_out), .Q(j_k_ff_1_q));  // open: K, Qn, preset, reset
  J_K_Flip_Flop j_k_ff_2 (.J(or_2_out), .clk(clock_1_out), .Q(j_k_ff_2_q));  // open: K, Qn, preset, reset
  J_K_Flip_Flop j_k_ff_3 (.J(not_1_out), .clk(clock_1_out), .Q(j_k_ff_3_q));  // open: K, Qn, preset, reset
  or or_1 (or_1_out, and_1_out, and_2_out);
  or or_2 (or_2_out, and_3_out, and_4_out);
  and and_1 (and_1_out, j_k_ff_1_q, ~j_k_ff_3_q);  // AND_Gate
  and and_2 (and_2_out, ~j_k_ff_2_q, ~j_k_ff_1_q, j_k_ff_3_q);  // AND_Gate
  and and_3 (and_3_out, j_k_ff_2_q, ~j_k_ff_3_q);  // AND_Gate
  and and_4 (and_4_out, j_k_ff_2_q, j_k_ff_1_q);
  not not_1 (not_1_out, j_k_ff_3_q);
endmodule
